# Fritzing sketch electricCircuit (saved by Fritzing 0.9.10b)
breadboards: 1

parts:
  Part2 = Arduino Nano (Rev3.0) (ICSP)
  LED1 = LED - 5mm [color="Red (633nm)" current=0.030 package="5 mm [THT]"]
  LED2 = LED - 5mm [color="Yellow (585nm)" current=0.030 package="5 mm [THT]"]
  LED3 = LED - 5mm [color="Green (570nm)" current=0.030 package="5 mm [THT]"]
  R1 = Resistor [tolerance=±5% power=0.25 resistance=10000 package=THT]
  R2 = Resistor [tolerance=±5% power=0.25 resistance=10000 package=THT]
  R3 = Resistor [tolerance=±5% power=0.25 resistance=10000 package=THT]
  HC-SR04_Sensor_1 = HC-SR04 Ultrasonic Distance Sensor
  HC-SR04_Sensor_2 = HC-SR04 Ultrasonic Distance Sensor
  HC-SR04_Sensor_3 = HC-SR04 Ultrasonic Distance Sensor

nets:
  GND: Part2.GND, HC-SR04_Sensor_1.GND, HC-SR04_Sensor_2.GND, HC-SR04_Sensor_3.GND
  N1: Part2.D5, R3.Pin_1
  N2: Part2.D6, R2.Pin_1
  N3: Part2.D7, R1.Pin_1
  VCC: Part2.5V, LED1.cathode, LED2.cathode, LED3.cathode, HC-SR04_Sensor_1.VCC, HC-SR04_Sensor_2.VCC, HC-SR04_Sensor_3.VCC
  N4: Part2.A5, HC-SR04_Sensor_3.ECHO
  N5: Part2.A4, HC-SR04_Sensor_3.TRIG
  N6: Part2.A3, HC-SR04_Sensor_2.ECHO
  N7: Part2.A2, HC-SR04_Sensor_2.TRIG
  N8: Part2.A1, HC-SR04_Sensor_1.ECHO
  N9: Part2.A0, HC-SR04_Sensor_1.TRIG
  N10: LED1.anode, R1.Pin_0
  N11: LED2.anode, R2.Pin_0
  N12: LED3.anode, R3.Pin_0
